// Digital circuit ALU.dig as structural Verilog
module ALU (
  input  [31:0] B,
  input  [31:0] A,
  input  Carry_in,
  input  [2:0] OPCODE,
  output [31:0] RESULT,
  output Overflow,
  output Negative,
  output Carry_out,
  output Zero
);

  wire add_1_c_o, bitselector_1_out, bitselector_3_out, comparator_1_eq, not_1_out, overflowaddition_1_o,
       overflowsubtraction_1_o, sub_1_c_o;
  wire [31:0] add_1_s, and_1_out, and_2_out, barrelshifter_1_out, or_1_out, sub_1_s, xor_1_out;

  // Probe A on A
  // Probe B on B
  // Probe OPCODE on OPCODE
  Sub #(.Bits(32)) sub_1 (.a(A), .b(B), .c_i(Carry_in), .s(sub_1_s), .c_o(sub_1_c_o));
  Add #(.Bits(32)) add_1 (.a(A), .b(B), .c_i(Carry_in), .s(add_1_s), .c_o(add_1_c_o));
  BarrelShifter #(.Bits(32), .barrelShifterMode("rotate"), .barrelSigned("true")) barrelshifter_1 (
    .in(B), .shift(A[6:0]), .out(barrelshifter_1_out));
  assign and_1_out = A & ~B;  // And and_1, 32 bits wide
  assign and_2_out = A & B;  // And and_2, 32 bits wide
  assign xor_1_out = A ^ B;  // XOr xor_1, 32 bits wide
  assign or_1_out = A | B;  // Or or_1, 32 bits wide
  Multiplexer #(.Selector_Bits(3), .Bits(32)) multiplexer_1 (
    .sel(OPCODE), .in_0(or_1_out), .in_1(xor_1_out), .in_2(and_2_out), .in_3(and_1_out), .in_4({32{1'b0}}),
    .in_5(barrelshifter_1_out), .in_6(add_1_s), .in_7(sub_1_s), .out(RESULT));
  BitSelector #(.Selector_Bits(5)) bitselector_1 (.in(B), .sel({5{1'b1}}), .out(bitselector_1_out));
  Comparator #(.Signed("true")) comparator_1 (
    .a(bitselector_1_out), .b(Negative), .eq(comparator_1_eq));  // open: gt, lt
  BitSelector #(.Selector_Bits(5)) bitselector_2 (.in(RESULT), .sel({5{1'b1}}), .out(Negative));
  Multiplexer #(.Selector_Bits(3)) multiplexer_2 (
    .sel(OPCODE), .in_0(1'b0), .in_1(1'b0), .in_2(1'b0), .in_3(1'b0), .in_4(1'b0), .in_5(bitselector_3_out),
    .in_6(add_1_c_o), .in_7(sub_1_c_o), .out(Carry_out));
  BitSelector #(.Selector_Bits(5)) bitselector_3 (.in(RESULT), .sel({5{1'b0}}), .out(bitselector_3_out));
  Comparator #(.Signed("true"), .Bits(32)) comparator_2 (.a(RESULT), .b({32{1'b0}}), .eq(Zero));  // open: gt, lt
  not not_1 (not_1_out, comparator_1_eq);
  OverflowAddition overflowaddition_1 (.A(A), .B(B), ._31Res(Negative), .O(overflowaddition_1_o));
  // Probe RESULT on RESULT
  OverflowSubtraction overflowsubtraction_1 (.A(A), .B(B), ._31Res(Negative), .O(overflowsubtraction_1_o));
  Multiplexer #(.Selector_Bits(3)) multiplexer_3 (
    .sel(OPCODE), .in_0(1'b0), .in_1(1'b0), .in_2(1'b0), .in_3(1'b0), .in_4(1'b0), .in_5(not_1_out),
    .in_6(overflowaddition_1_o), .in_7(overflowsubtraction_1_o), .out(Overflow));
endmodule
