// Digital circuit C10toC32.dig as structural Verilog
module C10toC32 (
  input  [9:0] C10,
  output [31:0] C32
);

  Multiplexer #(.Bits(32)) multiplexer_1 (.sel(C10[9]), .in_0({{22{1'b0}}, C10}), .in_1({{22{1'b1}}, C10}), .out(C32));
endmodule
