// Digital circuit Computer.dig as structural Verilog
module Computer (
  input  CLOCK
);

  wire and_1_out, and_2_out, comparator_1_eq, cpu_1_halted, cpu_1_nre, cpu_1_nwe, delay_1_out, nor_1_out,
       nor_2_out, not_1_out, not_2_out, nRESET_out;
  wire [15:0] cpu_1_addressbus_2, keyboard_1_d;
  wire [31:0] cpu_1_addressbus, cpu_1_databus_out, multiplexer_1_out, RAM_d;

  Reset nRESET (.out(nRESET_out));
  CPU cpu_1 (
    .DATABUS_IN(multiplexer_1_out), .CLOCK(CLOCK), .nRESET(nRESET_out),
    .ADDRESSBUS({cpu_1_addressbus[31:18], cpu_1_addressbus_2, cpu_1_addressbus[1:0]}),
    .DATABUS_OUT(cpu_1_databus_out), .nRE(cpu_1_nre), .nWE(cpu_1_nwe), .HALTED(cpu_1_halted));
  Delay delay_1 (.in(CLOCK), .out(delay_1_out));
  Comparator #(.Signed("true"), .Bits(32)) comparator_1 (
    .a({cpu_1_addressbus[31:18], cpu_1_addressbus_2, cpu_1_addressbus[1:0]}), .b(32'hfffffe00),
    .eq(comparator_1_eq));  // open: gt, lt
  nor nor_1 (nor_1_out, comparator_1_eq, cpu_1_nwe);
  nor nor_2 (nor_2_out, comparator_1_eq, cpu_1_nre);
  RAMDualPort #(.AddrBits(16), .isProgramMemory("true"), .Bits(32)) RAM (
    .A(cpu_1_addressbus_2), .Din(cpu_1_databus_out), .str(nor_1_out), .C(delay_1_out), .ld(nor_2_out),
    .D(RAM_d));
  not not_1 (not_1_out, cpu_1_nre);
  Multiplexer #(.Bits(32)) multiplexer_1 (
    .sel(nor_2_out), .in_0({{16{1'b0}}, keyboard_1_d}), .in_1(RAM_d), .out(multiplexer_1_out));
  and and_1 (and_1_out, comparator_1_eq, not_1_out);
  Keyboard keyboard_1 (.C(delay_1_out), .en(and_1_out), .D(keyboard_1_d));  // open: av
  not not_2 (not_2_out, cpu_1_nwe);
  and and_2 (and_2_out, comparator_1_eq, not_2_out);
  Terminal terminal_1 (.D(cpu_1_databus_out), .C(delay_1_out), .en(and_2_out));
  // Probe halted on cpu_1_halted
  // Probe nRE on cpu_1_nre
  // Probe nWE on cpu_1_nwe
  // Probe databusToCPU on multiplexer_1_out
  // Probe databusFromCPU on cpu_1_databus_out
  // Probe addressbus on {cpu_1_addressbus[31:18], cpu_1_addressbus_2, cpu_1_addressbus[1:0]}
  // Probe address_IO on comparator_1_eq

  // Notes on the sheet:
  //   CLOCK: Hz: 50
  //   Original Hades design by David N. Jansen, Radboud Universiteit Nijmegen, Nederland (2012)
  //   Ported to Digital and modified by Ciske Harsema (2019)
endmodule
