// Digital circuit FlagRegisterBank.dig as structural Verilog
// The RUN1920 CPU FlagRegisterBank component
module FlagRegisterBank (
  input  OVERFLOW_IN,
  input  NEGATIVE_IN,
  input  CARRY_IN,
  input  ZERO_IN,
  input  SetFlags,
  input  CLOCK,
  input  nRESET,
  output OVERFLOW_OUT,
  output NEGATIVE_OUT,
  output CARRY_OUT,
  output ZERO_OUT
);

  // RegRE regre_1: pin names not known; wires that end beside it: SetFlags, OVERFLOW_IN, CLOCK, nRESET, OVERFLOW_OUT
  // RegRE regre_2: pin names not known; wires that end beside it: SetFlags, NEGATIVE_IN, CLOCK, nRESET, NEGATIVE_OUT
  // RegRE regre_3: pin names not known; wires that end beside it: SetFlags, CARRY_IN, CLOCK, nRESET, CARRY_OUT
  // RegRE regre_4: pin names not known; wires that end beside it: SetFlags, ZERO_IN, CLOCK, nRESET, ZERO_OUT
endmodule
