// Digital circuit Inc4A.dig as structural Verilog
module Inc4A (
  input  [31:0] D,
  output [31:0] Q
);

  Add #(.Bits(30)) add_1 (.a(D[31:2]), .b(30'h1), .c_i(1'b0), .s(Q[31:2]));  // open: c_o

  assign Q[1:0] = 2'b00;
endmodule

/* Test case randomTests:
D Q
loop(i, 10000)
  let a = random(1<<30);
  (a) ((a&~3)+4)
end loop
*/

/* Test case 8bitTests:
D Q
repeat(256) (n) ((n&~3)+4)
*/
