// Digital circuit InstructionDecoder.dig as structural Verilog
// The RUN1920 CPU InstructionDecoder component
module InstructionDecoder (
  input  [31:0] INSTRUCTION,
  input  CLOCK,
  input  EXECUTE,
  input  FETCH,
  input  nRESET,
  output nWRITE,
  output PUSH,
  output nREAD,
  output POP,
  output [3:0] ADDR_DEST,
  output [3:0] ADDR_B,
  output [3:0] ADDR_A,
  output [31:0] CONSTANT,
  output LOADHI,
  output USE_CONSTANT,
  output [2:0] OPCODE,
  output SetFlags,
  output [3:0] CONDITION,
  output HALT
);

  wire and_1_out, comparator_1_eq, comparator_4_eq, comparator_6_eq, nor_1_out, or_5_out;
  wire [2:0] multiplexer_2_out;
  wire [31:0] c10toc32_1_c32, c22toc32_1_c32, multiplexer_1_out, multiplexer_3_out;
  wire [31:4] regre_1_p5;

  // RegRE #(.Bits(32)) regre_1: pin names not known; wires that end beside it: FETCH, INSTRUCTION, CLOCK, nRESET, {regre_1_p5, CONDITION}
  Multiplexer #(.Bits(32)) multiplexer_1 (
    .sel(EXECUTE), .in_0({32{1'b0}}), .in_1({regre_1_p5, CONDITION}),
    .out({multiplexer_1_out[31:16], ADDR_A, ADDR_B, ADDR_DEST, multiplexer_1_out[3:0]}));
  Multiplexer #(.Bits(3)) multiplexer_2 (
    .sel(multiplexer_1_out[31]), .in_0(multiplexer_1_out[30:28]), .in_1(3'b110), .out(multiplexer_2_out));
  and and_1 (and_1_out, ~multiplexer_1_out[31], multiplexer_1_out[27]);  // And
  Comparator #(.Bits(32)) comparator_1 (
    .a({multiplexer_1_out[31:16], ADDR_A, ADDR_B, ADDR_DEST, multiplexer_1_out[3:0]}), .b({32{1'b0}}),
    .eq(comparator_1_eq));  // open: gt, lt
  Comparator #(.Bits(6)) comparator_2 (.a(multiplexer_1_out[31:26]), .b({6{1'b1}}), .eq(HALT));  // open: gt, lt
  Comparator #(.Bits(6)) comparator_3 (.a(multiplexer_1_out[31:26]), .b(6'b110100), .eq(POP));  // open: gt, lt
  Comparator #(.Bits(6)) comparator_4 (
    .a(multiplexer_1_out[31:26]), .b(6'b110000), .eq(comparator_4_eq));  // open: gt, lt
  Comparator #(.Bits(6)) comparator_5 (.a(multiplexer_1_out[31:26]), .b(6'b110001), .eq(PUSH));  // open: gt, lt
  Comparator #(.Bits(6)) comparator_6 (
    .a(multiplexer_1_out[31:26]), .b(6'b111000), .eq(comparator_6_eq));  // open: gt, lt
  nor nor_1 (nor_1_out, multiplexer_1_out[31], multiplexer_1_out[26]);
  Comparator #(.Bits(2)) comparator_7 (.a(2'b10), .b(multiplexer_1_out[31:30]), .eq(LOADHI));  // open: gt, lt
  C10toC32 c10toc32_1 (.C10(multiplexer_1_out[25:16]), .C32(c10toc32_1_c32));
  C22toC32 c22toc32_1 (.C22({multiplexer_1_out[29:16], ADDR_A, ADDR_B}), .C32(c22toc32_1_c32));
  or or_1 (SetFlags, and_1_out, multiplexer_1_out[31], comparator_1_eq);
  or or_2 (USE_CONSTANT, comparator_4_eq, comparator_6_eq, nor_1_out);
  or or_3 (nREAD, POP, comparator_4_eq);
  or or_4 (nWRITE, PUSH, comparator_6_eq);
  Multiplexer #(.Bits(32)) multiplexer_3 (
    .sel(USE_CONSTANT), .in_0({32{1'b0}}), .in_1(c10toc32_1_c32), .out(multiplexer_3_out));
  Multiplexer #(.Bits(32)) multiplexer_4 (
    .sel(LOADHI), .in_0(multiplexer_3_out), .in_1(c22toc32_1_c32), .out(CONSTANT));
  Multiplexer #(.Bits(3)) multiplexer_5 (.sel(or_5_out), .in_0(multiplexer_2_out), .in_1(3'b110), .out(OPCODE));
  or or_5 (or_5_out, nWRITE, nREAD);
endmodule
