// Digital circuit OverflowAddition.dig as structural Verilog
module OverflowAddition (
  input  [31:0] A,
  input  [31:0] B,
  input  _31Res,
  output O
);

  wire and_1_out, and_2_out, and_3_out, bitselector_1_out, bitselector_2_out, nor_1_out, not_1_out;

  BitSelector #(.Selector_Bits(5)) bitselector_1 (.in(A), .sel({5{1'b1}}), .out(bitselector_1_out));
  BitSelector #(.Selector_Bits(5)) bitselector_2 (.in(B), .sel({5{1'b1}}), .out(bitselector_2_out));
  nor nor_1 (nor_1_out, bitselector_1_out, bitselector_2_out);
  not not_1 (not_1_out, _31Res);
  and and_1 (and_1_out, bitselector_1_out, bitselector_2_out);
  and and_2 (and_2_out, nor_1_out, _31Res);
  and and_3 (and_3_out, and_1_out, not_1_out);
  or or_1 (O, and_3_out, and_2_out);
endmodule
