// Digital circuit RegRESP.dig as structural Verilog
module RegRESP (
  input  en,
  input  [31:0] D,
  input  C,
  input  nR,
  input  pop,
  output [31:0] Q
);

  wire or_1_out;
  wire [31:0] inc4a_1_q, multiplexer_1_out;

  Inc4A inc4a_1 (.D(Q), .Q(inc4a_1_q));
  Multiplexer #(.Bits(32)) multiplexer_1 (.sel(pop), .in_0(D), .in_1(inc4a_1_q), .out(multiplexer_1_out));
  or or_1 (or_1_out, pop, en);
  // RegRE #(.Bits(32)) R14: pin names not known; wires that end beside it: or_1_out, multiplexer_1_out, C, nR, Q
endmodule
