// Digital circuit RegisterBank.dig as structural Verilog
// The RUN1920 CPU RegisterBank component
module RegisterBank (
  input  [31:0] DATA,
  input  POP,
  input  [3:0] ADDR_DEST,
  input  [3:0] ADDR_B,
  input  [3:0] ADDR_A,
  input  nRESET,
  input  CLOCK,
  output [31:0] REG_B,
  output [31:0] REG_A
);

  wire decoder_1_out_1, decoder_1_out_2, decoder_1_out_3, decoder_1_out_4, decoder_1_out_5, decoder_1_out_6,
       decoder_1_out_7, decoder_1_out_8, decoder_1_out_9, decoder_1_out_10, decoder_1_out_11, R12_p1, R13_p1,
       R14_p1, R15_p1;
  wire [31:0] R0_p8, R1_p5, R2_p5, R3_p5, R4_p5, R5_p5, R6_p5, R7_p5, R8_p5, R9_p5, R10_p5, R11_p5, R12_p5,
       R13_p5, R14_p6, R15_p5;

  // Probe ADDR-DEST on ADDR_DEST
  // Probe DATA on DATA
  // Probe POP on POP
  // RegRE #(.Bits(32)) R12: pin names not known; wires that end beside it: R12_p1, DATA, CLOCK, nRESET, R12_p5
  // RegRE #(.Bits(32)) R13: pin names not known; wires that end beside it: R13_p1, DATA, CLOCK, nRESET, R13_p5
  // RegRESP R14: pin names not known; wires that end beside it: R14_p1, DATA, CLOCK, nRESET, POP, R14_p6
  // RegRE #(.Bits(32), .isProgramCounter("true")) R15: pin names not known; wires that end beside it: R15_p1, DATA, CLOCK, nRESET, R15_p5
  Decoder #(.Selector_Bits(4)) decoder_1 (
    .sel(ADDR_DEST), .out_1(decoder_1_out_1), .out_2(decoder_1_out_2), .out_3(decoder_1_out_3),
    .out_4(decoder_1_out_4), .out_5(decoder_1_out_5), .out_6(decoder_1_out_6), .out_7(decoder_1_out_7),
    .out_8(decoder_1_out_8), .out_9(decoder_1_out_9), .out_10(decoder_1_out_10), .out_11(decoder_1_out_11),
    .out_12(R12_p1), .out_13(R13_p1), .out_14(R14_p1), .out_15(R15_p1));  // open: out_0
  // RegRE #(.Bits(32)) R8: pin names not known; wires that end beside it: decoder_1_out_8, DATA, CLOCK, nRESET, R8_p5
  // RegRE #(.Bits(32)) R9: pin names not known; wires that end beside it: decoder_1_out_9, DATA, CLOCK, nRESET, R9_p5
  // RegRE #(.Bits(32)) R10: pin names not known; wires that end beside it: decoder_1_out_10, DATA, CLOCK, nRESET, R10_p5
  // RegRE #(.Bits(32)) R11: pin names not known; wires that end beside it: decoder_1_out_11, DATA, CLOCK, nRESET, R11_p5
  // RegRE #(.Bits(32)) R4: pin names not known; wires that end beside it: decoder_1_out_4, DATA, CLOCK, nRESET, R4_p5
  // RegRE #(.Bits(32)) R5: pin names not known; wires that end beside it: decoder_1_out_5, DATA, CLOCK, nRESET, R5_p5
  // RegRE #(.Bits(32)) R6: pin names not known; wires that end beside it: decoder_1_out_6, DATA, CLOCK, nRESET, R6_p5
  // RegRE #(.Bits(32)) R7: pin names not known; wires that end beside it: decoder_1_out_7, DATA, CLOCK, nRESET, R7_p5
  // RegRE #(.Bits(32)) R0: pin names not known; wires that end beside it: 1'b0, DATA, CLOCK, nRESET, DATA, CLOCK, nRESET, R0_p8
  // RegRE #(.Bits(32)) R1: pin names not known; wires that end beside it: decoder_1_out_1, DATA, CLOCK, nRESET, R1_p5
  // RegRE #(.Bits(32)) R2: pin names not known; wires that end beside it: decoder_1_out_2, DATA, CLOCK, nRESET, R2_p5
  // RegRE #(.Bits(32)) R3: pin names not known; wires that end beside it: decoder_1_out_3, DATA, CLOCK, nRESET, R3_p5
  Multiplexer #(.Selector_Bits(4), .Bits(32)) multiplexer_1 (
    .sel(ADDR_A), .in_0(R0_p8), .in_1(R1_p5), .in_2(R2_p5), .in_3(R3_p5), .in_4(R4_p5), .in_5(R5_p5),
    .in_6(R6_p5), .in_7(R7_p5), .in_8(R8_p5), .in_9(R9_p5), .in_10(R10_p5), .in_11(R11_p5), .in_12(R12_p5),
    .in_13(R13_p5), .in_14(R14_p6), .in_15(R15_p5), .out(REG_A));
  // Probe ADDR-A on ADDR_A
  Multiplexer #(.Selector_Bits(4), .Bits(32)) multiplexer_2 (
    .sel(ADDR_B), .in_0(R0_p8), .in_1(R1_p5), .in_2(R2_p5), .in_3(R3_p5), .in_4(R4_p5), .in_5(R5_p5),
    .in_6(R6_p5), .in_7(R7_p5), .in_8(R8_p5), .in_9(R9_p5), .in_10(R10_p5), .in_11(R11_p5), .in_12(R12_p5),
    .in_13(R13_p5), .in_14(R14_p6), .in_15(R15_p5), .out(REG_B));
  // Probe ADDR-B on ADDR_B
endmodule
