// Digital circuit Tester.dig as structural Verilog
module Tester (
  input  Overflow,
  input  Negative,
  input  Carry,
  input  Zero,
  input  [3:0] Condition,
  output TestSucceeds
);

  wire and_1_out, and_2_out, comparator_1_eq, not_1_out, not_2_out, not_3_out, not_4_out, not_5_out,
       or_1_out, or_2_out;

  not not_1 (not_1_out, Zero);
  not not_2 (not_2_out, Carry);
  not not_3 (not_3_out, Negative);
  not not_4 (not_4_out, Overflow);
  and and_1 (and_1_out, not_1_out, Carry);
  or or_1 (or_1_out, Zero, not_2_out);
  Comparator comparator_1 (.a(Overflow), .b(Negative), .eq(comparator_1_eq));  // open: gt, lt
  not not_5 (not_5_out, comparator_1_eq);
  and and_2 (and_2_out, not_1_out, comparator_1_eq);
  or or_2 (or_2_out, Zero, not_5_out);
  Multiplexer #(.Selector_Bits(4)) multiplexer_1 (
    .sel(Condition), .in_0(Zero), .in_1(not_1_out), .in_2(Carry), .in_3(not_2_out), .in_4(Negative),
    .in_5(not_3_out), .in_6(Overflow), .in_7(not_4_out), .in_8(and_1_out), .in_9(or_1_out),
    .in_10(comparator_1_eq), .in_11(not_5_out), .in_12(and_2_out), .in_13(or_2_out), .in_14(1'b0),
    .in_15(1'b1), .out(TestSucceeds));
endmodule
