// Digital circuit Timer.dig as structural Verilog
// The RUN1920 CPU Tester component
module Timer (
  input  HALT,
  input  CLOCK,
  input  nRESET_IN,
  input  TEST_SUCCEEDS,
  output EXECUTE,
  output FETCH,
  output nRESET_OUT,
  output HALTED
);

  wire and_1_out, and_2_out, check_q, delay_2_out, delay_nq, delay_q, execute_q, fetch_q, halted_nq,
       nand_1_out, nor_1_out, not_1_out, not_2_out, or_1_out, TEST_SUCCEEDS_p2;

  // ForcibleValue TEST_SUCCEEDS: pin names not known; wires that end beside it: TEST_SUCCEEDS, TEST_SUCCEEDS_p2
  not not_1 (not_1_out, nRESET_IN);
  and and_1 (and_1_out, EXECUTE, HALT);
  D_FF_AS check (.Set(1'b0), .D(1'b1), .C(CLOCK), .Clr(not_1_out), .Q(check_q));  // open: nQ
  or or_1 (or_1_out, HALTED, and_1_out);
  and and_2 (and_2_out, TEST_SUCCEEDS_p2, fetch_q);
  nand nand_1 (nand_1_out, fetch_q, TEST_SUCCEEDS_p2, 1'b1);
  D_FF_AS delay (.Set(1'b0), .D(check_q), .C(CLOCK), .Clr(not_1_out), .Q(delay_q), .nQ(delay_nq));
  not not_2 (not_2_out, CLOCK);
  D_FF_AS u_halted (.Set(1'b0), .D(or_1_out), .C(CLOCK), .Clr(delay_nq), .Q(HALTED), .nQ(halted_nq));
  D_FF_AS u_execute (.Set(1'b0), .D(and_2_out), .C(not_2_out), .Clr(delay_nq), .Q(execute_q));  // open: nQ
  D_FF_AS u_fetch (.Set(1'b0), .D(nand_1_out), .C(not_2_out), .Clr(delay_nq), .Q(fetch_q));  // open: nQ
  nor nor_1 (nor_1_out, CLOCK, delay_2_out);
  Delay delay_2 (.in(CLOCK), .out(delay_2_out));
  and and_3 (EXECUTE, halted_nq, execute_q, delay_q, nor_1_out);
  and and_4 (FETCH, halted_nq, fetch_q, delay_q, nor_1_out);
  and and_5 (nRESET_OUT, halted_nq, delay_q);

  // Notes on the sheet:
  //   conflict
  //   This timer has three extra features:
  //   1. If a test does not succeed, it skips the execution completely.
  //   2. It tries to pipeline the fetch and execute phases;
  //   however, if conflict==1 it does not do so.
  //   3. When the processor is halted, it sets nRESET-OUT to zero.
  //   As a result, the processor will stay in a defined state.
endmodule

/* Test case:
nRESET-IN CLOCK TEST-SUCCEEDS HALT nRESET-OUT FETCH EXECUTE HALTED
# init sequence
0 0 0 0 0 0 0 0
1 0 0 0 0 0 0 0
1 C 0 0 0 0 0 0

# check if at fetch
1 C 0 0 1 1 0 0

# test failed, check if remains at fetch
1 C 0 0 1 1 0 0

# test passed, check if at execute
1 C 1 0 1 0 1 0

# check if back to fetch
1 C 1 0 1 1 0 0

# halt
1 C 0 1 1 1 0 0
1 C 1 1 1 0 1 0
1 C 1 1 0 0 0 1

# check if stays halted
1 C 0 1 0 0 0 1
1 C 1 0 0 0 0 1
1 C 0 0 0 0 0 1
*/
